# Fritzing sketch connection_sketch_fritzing (saved by Fritzing 0.9.2b)

parts:
  S1 = Pushbutton [package="[SMD]"]
  WeMos_D1_R1 = WeMos D1 R2
  Part1 = LCD1602-I2C

nets:
  N1: S1.Pin_2, WeMos_D1_R1.GND#20
  N2: S1.Pin_4, WeMos_D1_R1.D8
  N3: WeMos_D1_R1.D14, Part1.SDA
  N4: WeMos_D1_R1.D15, Part1.SCL
  N5: WeMos_D1_R1.GND#21, Part1.GND
  5V: WeMos_D1_R1.5V, Part1.VCC

custom parts:
  WeMos D1 R2: The D1 R2 is a mini wifi board based on the ESP-8266EX.
  LCD1602-I2C: A standard character display, usually with 2x16 characters. Comes in many colors with LCM1602 IIC attached.
